// Logisim project activity 3 (221b312).circ as structural Verilog: 1 circuit, main circuit main
module main (
  input  in_1,
  input  in_2,
  input  in_3,
  input  in_4
);

  wire and_1_out, and_2_out, not_1_out, not_2_out, or_1_out, or_2_out, undriven, xor_1_out;

  xor xor_1 (xor_1_out, in_1, in_2);
  or or_1 (or_1_out, in_1, in_2);
  // OR_Gate or_2 has open pins: out=or_2_out
  and and_1 (and_1_out, in_1, in_2);
  // AND_Gate and_2 has open pins: out=and_2_out
  not not_1 (not_1_out, in_1);
  Multiplexer #(.select(2)) multiplexer_1 (
    .in0(not_1_out), .in1(and_1_out), .in2(or_1_out), .in3(xor_1_out));  // open: out, sel, en
  // NOT_Gate not_2 has open pins: in=open, out=not_2_out
  Multiplexer #(.select(2)) multiplexer_2 (
    .in0(not_2_out), .in1(and_2_out), .in2(or_2_out), .in3(undriven));  // open: out, sel, en
endmodule
